// Logisim project E4D.circ as structural Verilog: 1 circuit, main circuit main
module main (
  input  A,
  input  B,
  input  C,
  input  D,
  output out_5
);

  wire and_1_out, and_2_out, and_3_out;

  and and_1 (and_1_out, ~D, ~C, ~B, ~A);  // AND_Gate
  and and_2 (and_2_out, D, ~C, B, ~A);  // AND_Gate
  and and_3 (and_3_out, ~D, C, ~B, A);  // AND_Gate
  or or_1 (out_5, and_1_out, and_2_out, and_3_out);
endmodule
